# Fritzing sketch your-turn (saved by Fritzing 1.0.0)

parts:
  Breadboard = Breadboard  # not connected
  ESP32_TTGO_T-Display = ESP32 TTGO T-Display
  Potentiometer = Potentiometer
  Yellow_button = Yellow button
  Yellow_LED = Yellow LED
  220_ohm_resistor = 220 ohm resistor
  Joystick = Joystick
  Shared_3_3V_and_ground = Shared 3.3V and ground

nets:
  N1: ESP32_TTGO_T-Display.2, Yellow_button.Signal
  N2: ESP32_TTGO_T-Display.15, 220_ohm_resistor.B
  N3: ESP32_TTGO_T-Display.13, Potentiometer.2
  N4: ESP32_TTGO_T-Display.3V, Potentiometer.3, Joystick.3.3V, Shared_3_3V_and_ground.3V
  N5: ESP32_TTGO_T-Display.39, Joystick.VRx
  N6: ESP32_TTGO_T-Display.32, Joystick.VRy
  N7: ESP32_TTGO_T-Display.33, Joystick.SW
  GND: ESP32_TTGO_T-Display.G_R, Potentiometer.1, Yellow_button.GND, Yellow_LED.Cathode, Joystick.GND, Shared_3_3V_and_ground.G
  N8: Yellow_LED.Anode, 220_ohm_resistor.A

custom parts:
  Breadboard: Custom breadboard documentation part for Your Turn.
  ESP32 TTGO T-Display: Custom breadboard documentation part for Your Turn.
  Potentiometer: Custom breadboard documentation part for Your Turn.
  Yellow button: Custom breadboard documentation part for Your Turn.
  Yellow LED: Custom breadboard documentation part for Your Turn.
  220 ohm resistor: Custom breadboard documentation part for Your Turn.
  Joystick: Custom breadboard documentation part for Your Turn.
  Shared 3.3V and ground: Custom breadboard documentation part for Your Turn.
